# Fritzing sketch XL4016X2 (saved by Fritzing 0.9.3b)
perfboards: 7

parts:
  J1_SOLAR_PANEL = Screw terminal - 2 pins [package=THT]
  D2 = TVS Diode 47V [part_number=P6KE47CA]
  R1 = Resistor [tolerance=±5% resistance=100k package=THT]
  R2 = Resistor [tolerance=±5% resistance=15k package=THT]
  C1 = Ceramic Capacitor [capacitance=100nF package="100 mil [THT, multilayer]"]
  Part1 = ACS712 Low Current Sensor Board v12
  C1_1_LOW_ESR = Electrolytic Capacitor [capacitance=100µF voltage=50V package="100 mil [THT, electrolytic]"]
  C1_3 = Electrolytic Capacitor [capacitance=100µF voltage=50V package="100 mil [THT, electrolytic]"]
  C1_2 = Electrolytic Capacitor [capacitance=100µF voltage=50V package="100 mil [THT, electrolytic]"]
  C1_4 = Electrolytic Capacitor [capacitance=100µF voltage=50V package="100 mil [THT, electrolytic]"]
  J7_BATTERY = Screw terminal - 2 pins [package=THT]
  R3 = Resistor [tolerance=±5% resistance=100k package=THT]
  R4 = Resistor [tolerance=±5% resistance=47k package=THT]
  Part2 = ACS712 Low Current Sensor Board v12
  C6 = Ceramic Capacitor [capacitance=100nF package="100 mil [THT, multilayer]"]
  Fuse1 = Fuse with Handler [part_number=Htc-15m]
  U1 = MP2307Module [part_number=MP2307 package=THT]
  J2_BUCK1_IN = Screw terminal - 2 pins [package=THT]
  J5_BUCK2_IN = Screw terminal - 2 pins [package=THT]
  J4_BUCK1_OUT = Screw terminal - 2 pins [package=THT]
  J6_BUCK2_OUT = Screw terminal - 2 pins [package=THT]
  J3_LOAD = Screw terminal - 2 pins [package=THT]
  Q2_IRF4905 = Basic FET P-Channel [package="TO220 [THT]"]
  R2_2 = Resistor [tolerance=±5% resistance=100k package=THT]
  Q5 = NPN-Transistor [package="TO92 [THT]"]  # not connected
  R4_2 = Resistor [tolerance=±5% resistance=10k package=THT]
  D1 = Diode [package=diode-1n4148]
  D2_2 = Diode [package=diode-1n4148]
  Q4 = PNP-Transistor [package="TO92 [THT]"]
  R7 = Resistor [tolerance=±5% resistance=47k package=THT]
  Q3 = PNP-Transistor [package="TO92 [THT]"]
  R6 = Resistor [tolerance=±5% resistance=22k package=THT]  # not connected
  Q3_IRF4905 = Basic FET P-Channel [package="TO220 [THT]"]
  D5 = Diode [package=diode-1n4148]
  D6 = Diode [package=diode-1n4148]
  Q7 = PNP-Transistor [package="TO92 [THT]"]
  R10 = Resistor [tolerance=±5% resistance=47k package=THT]
  Q8 = PNP-Transistor [package="TO92 [THT]"]
  R9 = Resistor [tolerance=±5% resistance=22k package=THT]
  Q1_IRF4905 = Basic FET P-Channel [package="TO220 [THT]"]
  Q10_IRF4905 = Basic FET P-Channel [package="TO220 [THT]"]
  R11 = Resistor [tolerance=±5% resistance=100k package=THT]
  R12 = Resistor [tolerance=±5% resistance=10k package=THT]
  D8 = Diode [package=diode-1n4148]
  D9 = Diode [package=diode-1n4148]
  Q12 = PNP-Transistor [package="TO92 [THT]"]
  Q13 = NPN-Transistor [package="TO92 [THT]"]  # not connected
  R14 = Resistor [tolerance=±5% resistance=47k package=THT]
  Q11 = PNP-Transistor [package="TO92 [THT]"]
  R13 = Resistor [tolerance=±5% resistance=22k package=THT]
  Q9_IRF4905 = Basic FET P-Channel [package="TO220 [THT]"]
  J1_MAINS_INPUT_12V = Power Jack [package=power_jack_combo]
  Part3 = Arduino Nano (Rev3.0)
  J8_DS18B20 = screw terminal, 3 pins
  Part4 = MicroSD Card Module
  Part5 = Real Time Clock and EEPROM Module - DS1307 RTC and AT24C32 Eeprom
  U3 = XL4016Module [part_number=XL4016 package=THT]
  U2 = XL4016Module [part_number=XL4016 package=THT]
  R15 = Resistor [tolerance=±5% resistance=2.2k package=THT]
  D10 = Rectifier Diode [part_number=1N4148 package="300 mil [THT]"]
  R16 = Resistor [tolerance=±5% resistance=2.2k package=THT]
  D11 = Rectifier Diode [part_number=1N4148 package="300 mil [THT]"]
  LCD1 = LCD screen
  LCM1602_IIC1 = LCM1602 IIC [part_number="LCM1602 IIC" chip_label="LCM1602 IIC" package="DIP (Dual Inline) [THT]"]
  S1 = Momentary Switch [package=ksa_sealed_tac_switch]
  R17 = Resistor [tolerance=±5% resistance=10k package=THT]
  LED1 = LED - 3mm [color="Red (633nm)" package="3 mm [THT]"]
  LED2 = LED - 3mm [color="Green (570nm)" package="3 mm [THT]"]
  J11_LEDs = screw terminal, 3 pins
  R18 = Resistor [tolerance=±5% resistance=470 package=THT]
  R19 = Resistor [tolerance=±5% resistance=470 package=THT]

nets:
  N1: J1_SOLAR_PANEL.pin1, D2.anode
  N2: J1_SOLAR_PANEL.pin2, D2.cathode
  N3: R1.Pin_0, R2.Pin_1, C1.0, Part3.A0
  GND: R2.Pin_0, C1.1, Part1.GND, J7_BATTERY.pin1, R4.Pin_0, Part2.GND, C6.1, U1.IN-, U1.OUT-, J4_BUCK1_OUT.pin2, J6_BUCK2_OUT.pin2, J3_LOAD.pin2, R7.Pin_1, R10.Pin_1, R9.Pin_1, R14.Pin_1, R13.Pin_1, J1_MAINS_INPUT_12V.GNDBREAK, Part3.GND, J8_DS18B20.pin3, Part4.GND, Part5.GND, Part5.GND2, U3.OUT-, U2.OUT-, LCM1602_IIC1.GND, S1.1, S1.2, J11_LEDs.pin3
  N4: Part1.IP+, C1_1_LOW_ESR.+, C1_3.+, C1_2.+, C1_4.+, J2_BUCK1_IN.pin1, J5_BUCK2_IN.pin1, U3.IN+, U2.IN+
  5V: Part1.5V, Part2.5V, U1.OUT+, Part3.5V, J8_DS18B20.pin1, Part4.VCC, Part5.5V, Part5.Vcc, LCM1602_IIC1.VCC, R17.Pin_0
  N5: Part1.VO, Part3.A1
  N6: C1_1_LOW_ESR.-, C1_3.-, C1_2.-, C1_4.-, J2_BUCK1_IN.pin2, J5_BUCK2_IN.pin2, U3.IN-, U2.IN-
  N7: J7_BATTERY.pin2, Fuse1.Connector1
  N8: R3.Pin_0, R4.Pin_1, C6.0, Part3.A2
  N9: R3.Pin_1, Fuse1.Connector2, U1.IN+
  N10: Part2.IP+, Q10_IRF4905.drain
  N11: Part2.VO, Part3.A3
  N12: J4_BUCK1_OUT.pin1, Q1_IRF4905.drain, U2.OUT+
  N13: J6_BUCK2_OUT.pin1, Q3_IRF4905.drain, U3.OUT+
  N14: J3_LOAD.pin1, Q2_IRF4905.drain
  N15: Q2_IRF4905.gate, R2_2.Pin_1
  N16: Q2_IRF4905.source, R2_2.Pin_0, Q3_IRF4905.source, Q1_IRF4905.source
  N17: R4_2.Pin_1, Part3.D4
  N18: D1.C, Q3.E
  N19: D2_2.C, Q4.E
  N20: Q4.B, Q3.B, Q3.C
  N21: Q4.C, R7.Pin_0
  N22: Q3_IRF4905.gate, Q7.C, R10.Pin_0
  N23: D5.C, Q8.E
  N24: D6.C, Q7.E
  N25: Q7.B, Q8.B, Q8.C, R9.Pin_0
  N26: Q10_IRF4905.gate, R11.Pin_1
  N27: Q10_IRF4905.source, R11.Pin_0, Q9_IRF4905.source
  N28: R12.Pin_0, Part3.D3
  N29: D8.C, Q12.B, Q11.E, Q11.B, Q11.C, R13.Pin_0
  N30: D9.C, Q12.E
  N31: Q12.C, R14.Pin_0, Q9_IRF4905.gate
  N32: Q9_IRF4905.drain, J1_MAINS_INPUT_12V.PWR
  N33: Part3.D2, J8_DS18B20.pin2, Part5.DS, Part5.DS2
  N34: Part3.D6, R19.Pin_1
  N35: Part3.D8, Part4.CS
  N36: Part3.D9, R15.Pin_0
  N37: Part3.D10, R16.Pin_0
  N38: Part3.D11/MOSI, Part4.MOSI
  N39: Part3.D12/MISO, Part4.MISO
  N40: Part3.A6, S1.3, S1.4, R17.Pin_1
  N41: Part3.A5, Part5.SCL, Part5.SCL2, LCM1602_IIC1.SCL
  N42: Part3.A4, Part5.SDA, Part5.SDA2, LCM1602_IIC1.SDA
  N43: Part3.D13/SCK, Part4.SCK
  N44: U3.VADJ, D11.cathode
  N45: U2.VADJ, D10.cathode
  N46: R15.Pin_1, D10.anode
  N47: R16.Pin_1, D11.anode
  VSS: LCD1.VSS, LCM1602_IIC1.VSS
  VDD: LCD1.VDD, LCM1602_IIC1.VDD
  N48: LCD1.V0, LCM1602_IIC1.V0
  N49: LCD1.RS, LCM1602_IIC1.RS
  N50: LCD1.R/W, LCM1602_IIC1.RW
  N51: LCD1.E, LCM1602_IIC1.E
  N52: LCD1.DB0, LCM1602_IIC1.D0
  N53: LCD1.DB1, LCM1602_IIC1.D1
  N54: LCD1.DB2, LCM1602_IIC1.D2
  N55: LCD1.DB3, LCM1602_IIC1.D3
  N56: LCD1.DB4, LCM1602_IIC1.D4
  N57: LCD1.DB5, LCM1602_IIC1.D5
  N58: LCD1.DB6, LCM1602_IIC1.D6
  N59: LCD1.DB7, LCM1602_IIC1.D7
  N60: LCD1.LED+, LCM1602_IIC1.A
  N61: LCD1.LED-, LCM1602_IIC1.K
  N62: LED1.anode, LED2.anode
  N63: J11_LEDs.pin1, R19.Pin_0
  N64: J11_LEDs.pin2, R18.Pin_0

notes:
  to LED screw terminal

custom parts:
  TVS Diode 47V: A transient voltage suppressor diode
  MP2307Module: DC-DC converter based on MP2307 IC
  Real Time Clock and EEPROM Module - DS1307 RTC and AT24C32 Eeprom: This module provides a DS1307 Real Time Clock with battery backup and 4 kBytes of Eeprom. it needs a LIR2032 rechargeable Lithium coin cell battery which will run the module without external 5V power for many years. The DS1307 and Eeprom are accessed via the I2C protocol. Features: Two wire I2C interface Hour : Minutes : Seconds AM/PM Day Month, Date - Year Leap year compensation Accurate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
  XL4016Module: DC-DC converter based on XL4016 IC
  LCM1602 IIC: I2C-Module to use a 1602 or 2004 LCD on with the wire.h libory Serial LCD Modul
  Momentary Switch: Momentary Switch Button commonly used for reset or general input. Spark Fun Electronics SKU : COM-00097
